# Fritzing sketch circuit_diagram (saved by Fritzing 0.9.3b)
breadboards: 1

parts:
  WeMos_D1_Mini1 = WeMos D1 Mini
  Q1 = LTR-301 [package=ltr-301]
  VCC1 = Battery
  R1 = Resistor [tolerance=±5% resistance=220 package=THT]

nets:
  N1: WeMos_D1_Mini1.3V3, VCC1.+
  N2: WeMos_D1_Mini1.D5, R1.Pin_1
  N3: WeMos_D1_Mini1.G, Q1.E, VCC1.-
  N4: Q1.C, R1.Pin_0
